# Fritzing sketch ESP32_HCSR04 (saved by Fritzing 0.9.3b)
breadboards: 1

parts:
  ESP32-WROOM-32 = ESP32-38PinWide [part_number=ESP32]
  HC-SR04 = hc-sr04

nets:
  VIN: ESP32-WROOM-32.VIN, HC-SR04.VCC
  N1: ESP32-WROOM-32.GPIO2, HC-SR04.Echo
  N2: ESP32-WROOM-32.GPIO4, HC-SR04.Trig
  GND: ESP32-WROOM-32.GND, HC-SR04.GND

custom parts:
  ESP32-38PinWide: Generic 38-Pin ESP32 with wide format (only access to one side of pins on a breadboard) based on Stephen Lilley's HiLetgo ESP-WROOM-32 ESP32 ESP-32S Development Board.
