# Fritzing sketch ESP32_LIGHT (saved by Fritzing 0.9.3b)
breadboards: 1

parts:
  LIGHT-SENSOR = Light Sensor
  part = ESP32-38PinWide [part_number=ESP32-WROOM-32]

nets:
  VCC: LIGHT-SENSOR.VCC, part.VIN
  N1: LIGHT-SENSOR.AO, part.GPIO25
  N2: LIGHT-SENSOR.DO, part.GPIO26
  GND: LIGHT-SENSOR.GND, part.GND

custom parts:
  Light Sensor: This is a SN-LIGHT-MOD Light Sensor
  ESP32-38PinWide: Generic 38-Pin ESP32 with wide format (only access to one side of pins on a breadboard) based on Stephen Lilley's HiLetgo ESP-WROOM-32 ESP32 ESP-32S Development Board.
