# Fritzing sketch ESP32_DHT11 (saved by Fritzing 0.9.3b)
breadboards: 1

parts:
  ESP32-WROOM-32 = ESP32-38PinWide [part_number=ESP32]
  DHT1 = DHT11 Humitidy and Temperature Sensor

nets:
  N1: ESP32-WROOM-32.3.3, DHT1.VDD
  GND: ESP32-WROOM-32.GND, DHT1.GND
  N2: ESP32-WROOM-32.GPIO0, DHT1.DATA

custom parts:
  ESP32-38PinWide: Generic 38-Pin ESP32 with wide format (only access to one side of pins on a breadboard) based on Stephen Lilley's HiLetgo ESP-WROOM-32 ESP32 ESP-32S Development Board.
  DHT11 Humitidy and Temperature Sensor: DHT11 Humidity and Temperature Sensor
