# Fritzing sketch ESP32_PIR (saved by Fritzing 0.9.3b)
breadboards: 1

parts:
  ESP32-WROOM-32 = ESP32-38PinWide [part_number=ESP32]
  PIR = PIR sensor

nets:
  N1: ESP32-WROOM-32.3.3, PIR.VDD
  GND: ESP32-WROOM-32.GND, PIR.GND
  N2: ESP32-WROOM-32.GPIO5, PIR.SIG

custom parts:
  ESP32-38PinWide: Generic 38-Pin ESP32 with wide format (only access to one side of pins on a breadboard) based on Stephen Lilley's HiLetgo ESP-WROOM-32 ESP32 ESP-32S Development Board.
